# Fritzing sketch HMI_Relays_Raspi (saved by Fritzing 0.9.3b)

parts:
  U2 = 4-Channel 5v Relay Shield [package=relay-4ch5v10a]
  Part3 = Nextion LCD DRAFT [part_number=Nextion]
  Raspberry_Pi_1 = Raspberry Pi 3 [part_number=RPI-3-V1.2]
  Part4 = FTDI Basic Programmer

nets:
  VCC: U2.VCC, Raspberry_Pi_1.5V
  GND: U2.GND, Raspberry_Pi_1.GND
  N1: U2.IN1, Raspberry_Pi_1.GPIO16
  N2: U2.IN2, Raspberry_Pi_1.GPIO20
  N3: U2.IN4, Raspberry_Pi_1.GPIO26
  N4: U2.IN3, Raspberry_Pi_1.GPIO21
  N5: Part3.VCC, Part4.POWER
  N6: Part3.Tx, Part4.RXI
  N7: Part3.Rx, Part4.TXO
  GND_2: Part3.GND, Part4.GND

notes:
  HMI CONTROLS 4 RELAYS  WITH RASPBERRY PI
  TTL TO USB
  RELAY 4 CHANNEL
  RASPBERRY PI
  NEXTION HMI

custom parts:
  4-Channel 5v Relay Shield: 4 Channel 5v Relay Shield w. 2x SPD-06VDC-SD-C
  Nextion LCD DRAFT: Nextion HMI 2.4" TFT 320x240 resistive Lcd touch screen Intelligent Display Module for Arduino NX3224T024 4M Flash, 2KByte RAM, 65k colors
